# Fritzing sketch pcbschematic (saved by Fritzing 0.8.7b)
circuit board: 14.3718cm x 7.88188cm
breadboards: 1

parts:
  R1 = Resistor [tolerance=±5% resistance=10k package=THT]
  R2 = Resistor [tolerance=±5% resistance=10k package=THT]
  R3 = Resistor [tolerance=±5% resistance=10k package=THT]
  R4 = Resistor [tolerance=±5% resistance=10k package=THT]
  C1 = Electrolytic Capacitor [capacitance=1µF package="100 mil [THT, electrolytic]"]
  C2 = Electrolytic Capacitor [capacitance=1µF package="100 mil [THT, electrolytic]"]
  S1 = Pushbutton [package="[THT]"]
  R5 = Trimmer Potentiometer [maximum_resistance=10kΩ package=THT]
  Componente1 = Arduino Ethernet Shield (Rev3)
  BURDEN2 = Resistor [tolerance=±5% resistance=220 package=THT]
  DS1 = DS18B20 1-Wire Temperature Sensor [part_number=DS18B20]
  LCD1 = LCD screen
  U1 = 2.5mm Audio Jack [package=stereojack2.5mm_specia_pogopins]
  U2 = 2.5mm Audio Jack [package=stereojack2.5mm_specia_pogopins]
  BURDEN4 = Resistor [tolerance=±5% resistance=220 package=THT]

nets:
  N1: R1.Pin_0, R3.Pin_0, S1.Pin_1, S1.Pin_2, R5.leg1, Componente1.D8, DS1.VDD
  N2: R2.Pin_0, C1.+, BURDEN4.Pin_1
  N3: R2.Pin_1, C1.-
  N4: R4.Pin_0, C2.+, BURDEN2.Pin_1
  N5: R4.Pin_1, C2.-, S1.Pin_3, S1.Pin_4, R5.leg2, DS1.GND
  N6: R5.wiper, LCD1.V0
  GND: Componente1.GND, LCD1.VSS, LCD1.R/W
  N7: Componente1.A0, BURDEN2.Pin_0, U2.RIGHT
  N8: Componente1.A1, U1.RIGHT, BURDEN4.Pin_0
  N9: Componente1.A2, LCD1.DB5
  N10: Componente1.A3, LCD1.DB4
  N11: Componente1.A4/SDA, LCD1.E
  N12: Componente1.A5/SCL, LCD1.RS
  N13: Componente1.D2, LCD1.DB2
  N14: Componente1.PWM_D3, LCD1.DB7
  N15: Componente1.PWM_D5, LCD1.LED-
  N16: Componente1.PWM_D6, LCD1.DB3
  5V: Componente1.5V, LCD1.VDD, LCD1.DB6
