# Fritzing sketch pcbschematicrev (saved by Fritzing 0.8.7b)
circuit board: 17.2384cm x 11.8193cm
breadboards: 1

parts:
  R1 = Resistor [tolerance=±5% resistance=10k package=THT]
  R2 = Resistor [tolerance=±5% resistance=10k package=THT]
  R3 = Resistor [tolerance=±5% resistance=10k package=THT]
  R4 = Resistor [tolerance=±5% resistance=10k package=THT]
  C1 = Electrolytic Capacitor [capacitance=10µF voltage=16V package="100 mil [THT, electrolytic]"]
  C2 = Electrolytic Capacitor [capacitance=10µF voltage=16V package="100 mil [THT, electrolytic]"]
  S1 = Pushbutton [package="[THT]"]
  Componente1 = Arduino Ethernet Shield (Rev3)
  U1 = 2.5mm Audio Jack [package=stereojack2.5mm_specia_pogopins]
  U2 = 2.5mm Audio Jack [package=stereojack2.5mm_specia_pogopins]
  BURDEN4 = Resistor [tolerance=±5% resistance=13 package=THT]
  BURDEN5 = Resistor [tolerance=±5% resistance=13 package=THT]
  U3 = mystery part, 3 pins [chip_label=?]
  LCD1 = LCD screen
  R5 = Trimmer Potentiometer [maximum_resistance=10kΩ package=THT]
  Componente2 = Arduino Ethernet Shield (Rev3)
  R6 = Resistor [tolerance=±5% resistance=10k package=THT]

nets:
  N1: R1.Pin_0, R3.Pin_0, Componente1.5V, U3.pin3, R6.Pin_1
  N2: R1.Pin_1, R2.Pin_0, C1.+, U1.LEFT, BURDEN4.Pin_1
  N3: R2.Pin_1, C1.-
  N4: R3.Pin_1, R4.Pin_0, C2.+, U2.LEFT, BURDEN5.Pin_1
  N5: R4.Pin_1, C2.-, S1.Pin_3, S1.Pin_4, Componente1.D8, Componente1.GND, U3.pin2
  N6: S1.Pin_1, R6.Pin_0
  N7: Componente1.A0, U2.RIGHT, BURDEN5.Pin_0
  N8: Componente1.A1, U1.RIGHT, BURDEN4.Pin_0
  N9: Componente1.D7, U3.pin1
  VSS: LCD1.VSS, LCD1.R/W, R5.leg1, Componente2.GND
  VDD: LCD1.VDD, LCD1.DB6, R5.leg2, Componente2.5V
  N10: LCD1.V0, R5.wiper
  N11: LCD1.RS, Componente2.A5/SCL
  N12: LCD1.E, Componente2.A4/SDA
  N13: LCD1.DB2, Componente2.D2
  N14: LCD1.DB3, Componente2.PWM_D6
  N15: LCD1.DB4, Componente2.A3
  N16: LCD1.DB5, Componente2.A2
  N17: LCD1.DB7, Componente2.PWM_D3
  N18: LCD1.LED-, Componente2.PWM_D5
